# Fritzing sketch breaboard (saved by Fritzing 0.9.3b)
breadboards: 1

parts:
  Part1 = Arduino Uno (Rev3) - ICSP
  LED1 = LEDs [package=led10mm]
  IC1 = ULN2003A [package="DIP16 [THT]"]
  IC2 = ULN2003A [package="DIP16 [THT]"]
  LED2 = LEDs [package=led10mm]
  LED3 = LEDs [package=led10mm]
  LED4 = LEDs [package=led10mm]
  LED7 = LED - 5mm [color="Red (633nm)" package="5 mm [THT]"]
  R1 = Resistor [tolerance=±5% resistance=220 package=THT]
  R2 = Resistor [tolerance=±5% resistance=220 package=THT]
  R3 = Resistor [tolerance=±5% resistance=220 package=THT]
  R4 = Resistor [tolerance=±5% resistance=220 package=THT]
  R5 = Resistor [tolerance=±5% resistance=220 package=THT]
  R6 = Resistor [tolerance=±5% resistance=220 package=THT]
  7_Segment3 = 7 Segment Display
  S1 = Round Pushbutton
  Power_plug1 = Power plug
  R7 = Resistor [tolerance=±5% resistance=220 package=THT]

nets:
  N1: Part1.ICSP_MISO, Part1.D12/MISO, IC2.COM_-_Common
  N2: Part1.D8, IC2.Out_5
  N3: Part1.D9_PWM, IC1.In_1
  N4: Part1.D10_PWM/SS, IC2.Out_6
  N5: Part1.D11_PWM/MOSI, IC2.Out_7
  N6: Part1.D13/SCK, IC1.In_5
  N7: Part1.D1/TX, S1.leg0
  N8: Part1.D2, IC2.Out_2
  N9: Part1.D3_PWM, IC1.In_4
  N10: Part1.D4, IC2.Out_3
  N11: Part1.D5_PWM, IC1.In_3
  N12: Part1.D6_PWM, IC1.In_2
  N13: Part1.D7, IC2.Out_4
  N14: LED1.C, IC1.Out_1
  N15: LED1.A, IC1.COM_-_Common, IC2.In_1, LED2.A, LED3.A, LED4.A, LED7.cathode, 7_Segment3.common_anode, Power_plug1.VCC
  N16: IC1.0V, IC2.Out_1, S1.leg1, Power_plug1.GND
  N17: IC1.Out_5, LED7.anode
  N18: IC1.Out_4, LED4.C
  N19: IC1.Out_3, LED3.C
  N20: IC1.Out_2, LED2.C
  N21: IC2.In_2, R4.Pin_1
  N22: IC2.In_3, R5.Pin_1
  N23: IC2.In_4, R6.Pin_1
  N24: IC2.In_5, R7.Pin_0
  N25: IC2.In_6, R3.Pin_0
  N26: IC2.In_7, R2.Pin_0
  N27: IC2.0V, R1.Pin_0
  N28: R1.Pin_1, 7_Segment3.Segment_B, 7_Segment3.Segment_A, R7.Pin_1
  N29: R2.Pin_1, 7_Segment3.Segment_F
  N30: R3.Pin_1, 7_Segment3.Segment_G
  N31: R4.Pin_0, 7_Segment3.Segment_C
  N32: R5.Pin_0, 7_Segment3.Segment_D
  N33: R6.Pin_0, 7_Segment3.Segment_E

notes:
  12V Wall Adaptor
  1kOhm
  7-segment display
  Common Anode
  20mA max
  min 600Ohm
  12V 4W MR16 LEDs
  Big Red button+led
